# Fritzing sketch pi-zero-with-dht22 (saved by Fritzing 0.9.4)
breadboards: 1

parts:
  RHT1 = Humidity and Temperature Sensor RHT03
  R1 = Resistor [tolerance=±5% resistance=10k package="0603 [SMD]"]
  MCU1 = Raspberry Pi Zero

nets:
  N1: RHT1.Vcc, R1.Pin_0, MCU1.pin_1, MCU1.pin_17
  N2: RHT1.Data-signal, R1.Pin_1, MCU1.pin_22
  N3: RHT1.GND_2, MCU1.pin_6, MCU1.pin_34
